# Fritzing sketch Pedalino (saved by Fritzing 0.9.3b)
breadboards: 2

parts:
  LCD1 = LCD screen
  Componente1 = Arduino Mega 2560 (Rev3)
  Componente2 = Bluetooth HC-05 Macho
  Componente3 = IR Receiver Breakout [package=PCB]
  R2 = Resistor [tolerance=±5% resistance=1 package=THT]
  U1 = MIDI_CONN_FEMALE [package=din_5_female]
  S1 = Pushbutton [package="[THT]"]
  R6 = Rotary Potentiometer (Small) [maximum_resistance=100kΩ package=THT]
  S2 = Pushbutton [package="[THT]"]
  S3 = Pushbutton [package="[THT]"]
  S4 = Pushbutton [package="[THT]"]
  R3 = Rotary Potentiometer (Small) [maximum_resistance=10kΩ package=THT]
  LED1 = LED - 5mm [color="Blue (430nm)" package="5 mm [THT]"]
  R1 = Resistor [tolerance=±5% resistance=220 package=THT]
  R7 = Resistor [tolerance=±5% resistance=220 package=THT]
  R4 = Resistor [tolerance=±5% resistance=220 package=THT]

nets:
  GND: LCD1.VSS, LCD1.R/W, Componente1.GND, Componente2.GND, Componente3.GND, R2.Pin_0, U1.NC2, S1.Pin_1, S1.Pin_2, R6.leg1, S2.Pin_1, S2.Pin_2, S3.Pin_1, S3.Pin_2, S4.Pin_1, S4.Pin_2, R3.leg1, LED1.cathode, R1.Pin_0
  VCC: LCD1.VDD, Componente1.5V, Componente2.VCC, Componente3.VCC, R6.leg2, R3.leg2, R4.Pin_0
  N1: LCD1.V0, R2.Pin_1
  N2: LCD1.RS, Componente1.D53
  N3: LCD1.E, Componente1.D51
  N4: LCD1.DB4, Componente1.D49
  N5: LCD1.DB5, Componente1.D47
  N6: LCD1.DB6, Componente1.D45
  N7: LCD1.DB7, Componente1.D43
  N8: LCD1.LED+, Componente1.D41
  N9: LCD1.LED-, R1.Pin_1
  N10: Componente1.A0, R3.wiper
  N11: Componente1.A1, R6.wiper
  N12: Componente1.A2, S1.Pin_3, S1.Pin_4
  N13: Componente1.A3, S2.Pin_3, S2.Pin_4
  N14: Componente1.A4, S3.Pin_3, S3.Pin_4
  N15: Componente1.A5, S4.Pin_3, S4.Pin_4
  N16: Componente1.D17_PWM/RX2, Componente2.TXD
  N17: Componente1.D16_PWM/TX2, Componente2.RXD
  N18: Componente1.D14/TX3, U1.MIDI_OUT
  N19: Componente1.D33, Componente3.OUT
  N20: Componente1.D35, R7.Pin_0
  N21: U1.MIDI_IN, R4.Pin_1
  N22: LED1.anode, R7.Pin_1
